// Logisim project s-mips.circ as structural Verilog: 10 circuits, main circuit S-MIPS Board
module S_MIPS_Board (
  input  DESHABILITAR_DISPATCHER,
  output halt
);

  wire button_1_out, CLK, CS, d_ff_1_q, LCLR, LoadRAM, LoadRAMOn, LW, R_R_W, R_W, ram_dispatcher_1_finished,
       RCS, Reset_out, RST, TTY_EN;
  wire [2:0] KDB;
  wire [3:0] LMask, Mask, ram_1_read_time, ram_1_write_time, RMask;
  wire [6:0] KDB_DATA, TTY_DATA;
  wire [15:0] Addr, LAddr, RAddr;
  wire [31:0] I0, I1, I2, I3, LData, ram_1_data_out_0, ram_1_data_out_1, ram_1_data_out_2, ram_1_data_out_3,
       RI0, RI1, RI2, RI3;

  TTY #(.rows(25), .cols(80)) tty_1 (.data(TTY_DATA), .clk(CLK), .we(TTY_EN), .clr(RST));
  not not_1 (LoadRAMOn, ram_dispatcher_1_finished);
  RAM_Dispatcher ram_dispatcher_1 (
    .WriteTime(ram_1_write_time), .Clock(CLK), .Data(LData), .Address(LAddr), .Mask(LMask),
    .Finished(ram_dispatcher_1_finished), .Write(LW), .CLR(LCLR));
  Keyboard #(.buflen(64)) keyboard_1 (.clk(CLK), .re(KDB[0]), .avail(KDB[2]), .data(KDB_DATA));  // open: clr
  RAM ram_1 (
    .Address(RAddr), .Data_Out_0(ram_1_data_out_0), .Data_Out_1(ram_1_data_out_1),
    .Data_Out_2(ram_1_data_out_2), .Data_Out_3(ram_1_data_out_3), .Data_In_0(RI0), .Data_In_1(RI1),
    .Data_In_2(RI2), .Data_In_3(RI3), .Mask(RMask), .nRead_Write(R_R_W), .Chip_Select(RCS),
    .Read_Time(ram_1_read_time), .Reset(button_1_out), .Write_Time(ram_1_write_time));
  Button button_1 (.out(button_1_out));
  D_Flip_Flop d_ff_1 (.clk(CLK), .D(1'b1), .Q(d_ff_1_q), .reset(Reset_out));  // open: Qn, preset, en
  Button Reset (.out(Reset_out));
  S_MIPS s_mips_1 (
    .Kbd_Enable(KDB[0]), .Address(Addr), .Kbd_Clear(KDB[1]), .Kbd_Available(KDB[2]), .RAM_In_0(I0),
    .Kbd_ASCII_Data(KDB_DATA), .RAM_In_1(I1), .TTY_Enable(TTY_EN), .RAM_In_2(I2), .RAM_In_3(I3),
    .TTY_ASCII_Data(TTY_DATA), .Reset(RST), .RAM_Out_0(ram_1_data_out_0), .Clock(CLK),
    .RAM_Out_1(ram_1_data_out_1), .Stop(halt), .RAM_Out_2(ram_1_data_out_2), .RAM_Out_3(ram_1_data_out_3),
    .Mask(Mask), .Read_Time(ram_1_read_time), .Write_Time(ram_1_write_time), .nRead_Write(R_W),
    .Chip_Select(CS));
  D_Flip_Flop d_ff_2 (.clk(CLK), .D(d_ff_1_q), .Qn(LCLR), .reset(Reset_out));  // open: Q, preset, en
  or or_1 (RST, LCLR, LoadRAM);
  Clock clock_1 (.out(CLK));
  Multiplexer #(.width(32), .enable("false")) multiplexer_1 (.in0(I0), .in1(LData), .out(RI0), .sel(LoadRAM));
  Multiplexer #(.width(32), .enable("false")) multiplexer_2 (.in0(I1), .in1(LData), .out(RI1), .sel(LoadRAM));
  Multiplexer #(.width(32), .enable("false")) multiplexer_3 (.in0(I2), .in1(LData), .out(RI2), .sel(LoadRAM));
  Multiplexer #(.width(32), .enable("false")) multiplexer_4 (.in0(I3), .in1(LData), .out(RI3), .sel(LoadRAM));
  and and_1 (LoadRAM, ~DESHABILITAR_DISPATCHER, LoadRAMOn);  // AND_Gate
  Multiplexer #(.width(16), .enable("false")) multiplexer_5 (.in0(Addr), .in1(LAddr), .out(RAddr), .sel(LoadRAM));
  Multiplexer #(.width(4), .enable("false")) multiplexer_6 (.in0(Mask), .in1(LMask), .out(RMask), .sel(LoadRAM));
  Multiplexer #(.enable("false")) multiplexer_7 (.in0(CS), .in1(LW), .out(RCS), .sel(LoadRAM));
  Multiplexer #(.enable("false")) multiplexer_8 (.in0(R_W), .in1(LW), .out(R_R_W), .sel(LoadRAM));

  // Notes on the sheet:
  //   NO MODIFICAR
  //   Keyboard
endmodule

module RAM (
  input  [15:0] Address,
  input  [31:0] Data_In_0,
  input  [31:0] Data_In_1,
  input  [31:0] Data_In_2,
  input  [31:0] Data_In_3,
  input  [3:0] Mask,
  input  nRead_Write,
  input  Chip_Select,
  input  Reset,
  output [31:0] Data_Out_0,
  output [31:0] Data_Out_1,
  output [31:0] Data_Out_2,
  output [31:0] Data_Out_3,
  output [3:0] Read_Time,
  output [3:0] Write_Time
);

  wire and_2_out, and_3_out, and_4_out, and_5_out, and_6_out, and_7_out, and_8_out, and_9_out, Changed, CLK,
       comparator_2_eq, comparator_3_eq, comparator_4_eq, comparator_5_eq, comparator_6_eq, Count,
       demultiplexer_3_out0, Idle, Idle_q, Load, Load0, Load1, nand_1_out, or_1_out, or_2_out, or_3_out,
       or_4_out, or_5_out, or_6_out, or_7_out, or_8_out, or_9_out, or_10_out, Proc_q, Update_Mem, Zero_Time;
  wire [3:0] counter_1_q, multiplexer_1_out, subtractor_1_out;
  wire [31:0] register_1_q, register_2_q, register_3_q, register_4_q, register_5_q;

  // Probe on 4'b0011
  // Probe on 4'b0010
  Multiplexer #(.width(4), .enable("false")) multiplexer_1 (
    .in0(4'b0011), .in1(4'b0010), .out(multiplexer_1_out), .sel(nRead_Write));
  or or_1 (or_1_out, Idle, Update_Mem);
  or or_2 (or_2_out, ~Chip_Select, Reset);  // OR_Gate
  Subtractor #(.width(4)) subtractor_1 (.a(multiplexer_1_out), .b(4'b0010), .out(subtractor_1_out));  // open: bin, bout
  Demultiplexer #(.enable("false")) demultiplexer_1 (.out0(Idle), .out1(Load0), .in(Idle_q), .sel(Changed));
  D_Flip_Flop u_Idle (.clk(CLK), .D(or_1_out), .Q(Idle_q), .preset(or_2_out));  // open: Qn, en, reset
  // Probe on counter_1_q
  Counter #(.width(4), .max('hf)) counter_1 (
    .load(Load), .D(subtractor_1_out), .count(Count), .Q(counter_1_q), .clk(CLK), .clr(or_3_out));  // open: carry
  or or_3 (or_3_out, ~Chip_Select, Reset);  // OR_Gate
  Comparator #(.width(4), .mode("unsigned")) comparator_1 (
    .a(4'b0000), .b(counter_1_q), .eq(Zero_Time));  // open: gt, lt
  or or_4 (or_4_out, Count, Load0, Load1);
  Register #(.width(32)) register_1 (.D(Data_In_0), .en(Chip_Select), .Q(register_1_q), .clk(CLK), .clr(or_5_out));
  or or_5 (or_5_out, ~Chip_Select, Reset);  // OR_Gate
  Register #(.width(32)) register_2 (.D(Data_In_1), .en(Chip_Select), .Q(register_2_q), .clk(CLK), .clr(or_6_out));
  or or_6 (or_6_out, ~Chip_Select, Reset);  // OR_Gate
  Register #(.width(32)) register_3 (.D(Data_In_2), .en(Chip_Select), .Q(register_3_q), .clk(CLK), .clr(or_7_out));
  or or_7 (or_7_out, ~Chip_Select, Reset);  // OR_Gate
  Register #(.width(32)) register_4 (.D(Data_In_3), .en(Chip_Select), .Q(register_4_q), .clk(CLK), .clr(or_8_out));
  or or_8 (or_8_out, ~Chip_Select, Reset);  // OR_Gate
  Register #(.width(32)) register_5 (
    .D({{11{1'b1}}, nRead_Write, Mask, Address}), .en(Chip_Select), .Q(register_5_q), .clk(CLK),
    .clr(or_9_out));
  or or_9 (or_9_out, ~Chip_Select, Reset);  // OR_Gate
  D_Flip_Flop Proc (.clk(CLK), .D(or_4_out), .Q(Proc_q), .reset(or_10_out));  // open: Qn, preset, en
  or or_10 (or_10_out, ~Chip_Select, Reset);  // OR_Gate
  Demultiplexer #(.enable("false")) demultiplexer_2 (
    .out0(Count), .out1(Update_Mem), .in(demultiplexer_3_out0), .sel(Zero_Time));
  Demultiplexer #(.enable("false")) demultiplexer_3 (
    .out0(demultiplexer_3_out0), .out1(Load1), .in(Proc_q), .sel(Changed));
  Clock clock_1 (.out(CLK));
  Comparator #(.width(32)) comparator_2 (.a(register_1_q), .b(Data_In_0), .eq(comparator_2_eq));  // open: gt, lt
  Comparator #(.width(32)) comparator_3 (.a(register_2_q), .b(Data_In_1), .eq(comparator_3_eq));  // open: gt, lt
  Comparator #(.width(32)) comparator_4 (.a(register_3_q), .b(Data_In_2), .eq(comparator_4_eq));  // open: gt, lt
  Comparator #(.width(32)) comparator_5 (.a(register_4_q), .b(Data_In_3), .eq(comparator_5_eq));  // open: gt, lt
  Comparator #(.width(32)) comparator_6 (
    .a(register_5_q), .b({{11{1'b1}}, nRead_Write, Mask, Address}), .eq(comparator_6_eq));  // open: gt, lt
  nand nand_1 (nand_1_out, comparator_6_eq, comparator_2_eq, comparator_3_eq, comparator_4_eq, comparator_5_eq);
  and and_1 (Changed, nand_1_out, Chip_Select);
  or or_11 (Load, Count, Load1, Load0);
  and and_2 (and_2_out, Mask[0], Update_Mem, nRead_Write);
  and and_3 (and_3_out, Mask[1], Update_Mem, nRead_Write);
  and and_4 (and_4_out, Mask[2], Update_Mem, nRead_Write);
  and and_5 (and_5_out, Mask[3], Update_Mem, nRead_Write);
  RAM_part #(.addrWidth(16), .dataWidth(32), .bus("separate")) ram_1 (
    .addr(Address), .din(Data_In_0), .data(Data_Out_0), .str(and_2_out), .sel(Chip_Select), .clk(CLK),
    .ld(and_6_out), .clr(Reset));
  and and_6 (and_6_out, ~nRead_Write, Idle);  // AND_Gate
  RAM_part #(.addrWidth(16), .dataWidth(32), .bus("separate")) ram_2 (
    .addr(Address), .din(Data_In_1), .data(Data_Out_1), .str(and_3_out), .sel(Chip_Select), .clk(CLK),
    .ld(and_7_out), .clr(Reset));
  and and_7 (and_7_out, ~nRead_Write, Idle);  // AND_Gate
  RAM_part #(.addrWidth(16), .dataWidth(32), .bus("separate")) ram_3 (
    .addr(Address), .din(Data_In_2), .data(Data_Out_2), .str(and_4_out), .sel(Chip_Select), .clk(CLK),
    .ld(and_8_out), .clr(Reset));
  and and_8 (and_8_out, ~nRead_Write, Idle);  // AND_Gate
  RAM_part #(.addrWidth(16), .dataWidth(32), .bus("separate")) ram_4 (
    .addr(Address), .din(Data_In_3), .data(Data_Out_3), .str(and_5_out), .sel(Chip_Select), .clk(CLK),
    .ld(and_9_out), .clr(Reset));
  and and_9 (and_9_out, ~nRead_Write, Idle);  // AND_Gate

  assign Read_Time = 4'b0011;
  assign Write_Time = 4'b0010;

  // Other names for the same wires on the sheet: M0 = Mask[0]; M1 = Mask[1]; M2 = Mask[2]; M3 = Mask[3];
  //   RW = nRead_Write; CLR = Reset; CS = Chip_Select; Load2 = Count

  // Notes on the sheet:
  //   NO MODIFICAR
  //   excepto quizás los valores RT y WT
  //   BANK0
  //   BANK1
  //   BANK2
  //   BANK3
endmodule

module S_MIPS (
  input  Kbd_Available,
  input  [6:0] Kbd_ASCII_Data,
  input  [31:0] RAM_Out_0,
  input  [31:0] RAM_Out_1,
  input  Reset,
  input  [31:0] RAM_Out_2,
  input  Clock,
  input  [31:0] RAM_Out_3,
  input  [3:0] Read_Time,
  input  [3:0] Write_Time,
  output Kbd_Enable,
  output [15:0] Address,
  output Kbd_Clear,
  output TTY_Enable,
  output [6:0] TTY_ASCII_Data,
  output Stop,
  output [31:0] RAM_In_0,
  output [31:0] RAM_In_1,
  output [31:0] RAM_In_2,
  output [31:0] RAM_In_3,
  output [3:0] Mask,
  output nRead_Write,
  output Chip_Select
);


  // Other names for the same wires on the sheet: CLK = Clock; CLR = Reset; CS = Chip_Select;
  //   KBD_AVAIL = Kbd_Available; KBD_CLR = Kbd_Clear; KBD_DATA[6:0] = Kbd_ASCII_Data; RAM_A[15:0] = Address;
  //   RAM_INPUT_0[31:0] = RAM_In_0; RAM_INPUT_1[31:0] = RAM_In_1; RAM_INPUT_2[31:0] = RAM_In_2;
  //   RAM_INPUT_3[31:0] = RAM_In_3; RAM_MASK[3:0] = Mask; RAM_OUTPUT_0[31:0] = RAM_Out_0;
  //   RAM_OUTPUT_1[31:0] = RAM_Out_1; RAM_OUTPUT_2[31:0] = RAM_Out_2; RAM_OUTPUT_3[31:0] = RAM_Out_3;
  //   RW = nRead_Write; TTY_DATA[6:0] = TTY_ASCII_Data

  // Notes on the sheet:
  //   RAM ADDRESS
  //   DATA FROM RAM
  //   DATA TO RAM
  //   DATA WRITE MASK
  //   RAM TIMING
  //   RAM CONTROL
  //   KEYBOARD
  //   TTY
  //   SEQUENCING
endmodule

module RAM_Dispatcher (
  input  [3:0] WriteTime,
  input  Clock,
  input  CLR,
  output [31:0] Data,
  output [15:0] Address,
  output [3:0] Mask,
  output Finished,
  output Write
);

  wire demultiplexer_2_out1, demultiplexer_3_out1, End, IDLE_q, IncAddr, Load, or_1_out, or_2_out, While_q,
       WriteEnd;
  wire [3:0] counter_1_q;
  wire [31:0] CurrentAddress_q;

  Counter #(.width(32), .max('hffffffff)) CurrentAddress (
    .count(IncAddr), .Q({CurrentAddress_q[31:18], Address, CurrentAddress_q[1:0]}), .clr(CLR));  // open: load, D, carry, clk
  or or_1 (or_1_out, IncAddr, demultiplexer_3_out1, Finished);
  D_Flip_Flop IDLE (.clk(Clock), .D(or_1_out), .Q(IDLE_q), .preset(CLR));  // open: Qn, en, reset
  Demultiplexer #(.enable("false")) demultiplexer_1 (.out0(Load), .out1(Finished), .in(IDLE_q), .sel(End));
  D_Flip_Flop While (.clk(Clock), .D(or_2_out), .Q(While_q), .reset(CLR));  // open: Qn, preset, en
  or or_2 (or_2_out, Write, Load);
  RAM_part #(.addrWidth(18), .dataWidth(32)) ram_1 (
    .addr({Address, CurrentAddress_q[1:0]}), .data(Data), .clk(Clock));  // open: sel, ld, clr
  Demultiplexer #(.enable("false")) demultiplexer_2 (
    .out0(Write), .out1(demultiplexer_2_out1), .in(While_q), .sel(WriteEnd));
  Decoder #(.select(2)) decoder_1 (
    .out0(Mask[0]), .out1(Mask[1]), .out2(Mask[2]), .out3(Mask[3]), .sel(CurrentAddress_q[1:0]));  // open: en
  Demultiplexer #(.enable("false")) demultiplexer_3 (
    .out0(IncAddr), .out1(demultiplexer_3_out1), .in(demultiplexer_2_out1), .sel(End));
  Counter #(.width(4), .max('hf)) counter_1 (
    .load(Load), .D(WriteTime), .count(Write), .Q(counter_1_q), .clk(Clock));  // open: carry, clr
  Comparator #(.width(32)) comparator_1 (.a(Data), .b({32{1'b1}}), .eq(End));  // open: gt, lt
  Comparator #(.width(4)) comparator_2 (.a(4'b0000), .b(counter_1_q), .eq(WriteEnd));  // open: gt, lt

  // Other names for the same wires on the sheet: CLK = Clock; Count = Write; WT[3:0] = WriteTime
endmodule

module InstructionDecoder (
  input  [31:0] in_1,
  output [4:0] Output,
  output [5:0] Output_2,
  output [25:0] Output_3,
  output [4:0] Output_4,
  output [15:0] Output_5,
  output [4:0] Output_6,
  output Output_7,
  output Output_8,
  output Output_9,
  output Output_10,
  output Output_11,
  output Output_12,
  output Output_13,
  output Output_14,
  output Output_15,
  output Output_16,
  output Output_17,
  output Output_18,
  output Output_19,
  output Output_20,
  output Output_21,
  output Output_22,
  output Output_23,
  output Output_24,
  output Output_25,
  output Output_26,
  output Output_27,
  output Output_28,
  output Output_29,
  output Output_30,
  output Output_31,
  output Output_32,
  output Output_33,
  output Output_34,
  output Output_35,
  output Output_36,
  output Output_37,
  output Output_38,
  output Output_39,
  output Output_40,
  output Output_41,
  output Output_42
);

  wire _000000, _111111, comparator_16_eq, comparator_17_eq, comparator_18_eq, comparator_19_eq,
       comparator_20_eq, comparator_21_eq, comparator_22_eq, comparator_23_eq, comparator_24_eq,
       comparator_25_eq, comparator_26_eq, comparator_27_eq, comparator_28_eq, comparator_29_eq,
       comparator_30_eq, comparator_31_eq, comparator_32_eq, comparator_33_eq, comparator_34_eq,
       comparator_35_eq, comparator_36_eq, comparator_37_eq, comparator_38_eq, comparator_39_eq;

  Comparator #(.width(6)) comparator_1 (.a(in_1[31:26]), .b(6'b001000), .eq(Output_21));  // open: gt, lt
  Comparator #(.width(6)) comparator_2 (.a(in_1[31:26]), .b(6'b010010), .eq(Output_31));  // open: gt, lt
  Comparator #(.width(6)) comparator_3 (.a(in_1[31:26]), .b(6'b001010), .eq(Output_23));  // open: gt, lt
  Comparator #(.width(6)) comparator_4 (.a(in_1[31:26]), .b(6'b010001), .eq(Output_27));  // open: gt, lt
  Comparator #(.width(6)) comparator_5 (.a(in_1[31:26]), .b(6'b000100), .eq(Output_24));  // open: gt, lt
  Comparator #(.width(6)) comparator_6 (.a(in_1[31:26]), .b(6'b000101), .eq(Output_28));  // open: gt, lt
  Comparator #(.width(6)) comparator_7 (.a(in_1[31:26]), .b(6'b000110), .eq(Output_32));  // open: gt, lt
  Comparator #(.width(6)) comparator_8 (.a(in_1[31:26]), .b(6'b000111), .eq(Output_36));  // open: gt, lt
  Comparator #(.width(6)) comparator_9 (.a(in_1[31:26]), .b(6'b000001), .eq(Output_40));  // open: gt, lt
  Comparator #(.width(6)) comparator_10 (.a(in_1[31:26]), .b(6'b100011), .eq(Output_42));  // open: gt, lt
  Comparator #(.width(6)) comparator_11 (.a(in_1[31:26]), .b(6'b101011), .eq(Output_22));  // open: gt, lt
  Comparator #(.width(6)) comparator_12 (.a(in_1[31:26]), .b(6'b001101), .eq(Output_35));  // open: gt, lt
  Comparator #(.width(6)) comparator_13 (.a(in_1[31:26]), .b(6'b001110), .eq(Output_39));  // open: gt, lt
  Comparator #(.width(6)) comparator_14 (.a(in_1[31:26]), .b({6{1'b0}}), .eq(_000000));  // open: gt, lt
  Comparator #(.width(6)) comparator_15 (.a(in_1[31:26]), .b({6{1'b1}}), .eq(_111111));  // open: gt, lt
  Comparator #(.width(6)) comparator_16 (.a(in_1[5:0]), .b({6{1'b1}}), .eq(comparator_16_eq));  // open: gt, lt
  Comparator #(.width(6)) comparator_17 (.a(in_1[5:0]), .b(6'b000001), .eq(comparator_17_eq));  // open: gt, lt
  Comparator #(.width(6)) comparator_18 (.a(in_1[5:0]), .b(6'b000010), .eq(comparator_18_eq));  // open: gt, lt
  Comparator #(.width(6)) comparator_19 (.a(in_1[5:0]), .b(6'b000100), .eq(comparator_19_eq));  // open: gt, lt
  and and_1 (Output_26, _111111, comparator_16_eq);
  and and_2 (Output_30, _111111, comparator_17_eq);
  and and_3 (Output_34, _111111, comparator_18_eq);
  and and_4 (Output_38, _111111, comparator_19_eq);
  Comparator #(.width(6)) comparator_20 (.a(in_1[31:26]), .b(6'b111000), .eq(comparator_20_eq));  // open: gt, lt
  Comparator #(.width(6)) comparator_21 (.a(in_1[5:0]), .b({6{1'b0}}), .eq(comparator_21_eq));  // open: gt, lt
  Comparator #(.width(6)) comparator_22 (.a(in_1[31:26]), .b(6'b111000), .eq(comparator_22_eq));  // open: gt, lt
  Comparator #(.width(6)) comparator_23 (.a(in_1[5:0]), .b(6'b000001), .eq(comparator_23_eq));  // open: gt, lt
  and and_5 (Output_7, _000000, comparator_24_eq);
  Comparator #(.width(6)) comparator_24 (.a(in_1[5:0]), .b({6{1'b0}}), .eq(comparator_24_eq));  // open: gt, lt
  and and_6 (Output_9, _000000, comparator_25_eq);
  Comparator #(.width(6)) comparator_25 (.a(in_1[5:0]), .b(6'b100000), .eq(comparator_25_eq));  // open: gt, lt
  and and_7 (Output_11, _000000, comparator_26_eq);
  Comparator #(.width(6)) comparator_26 (.a(in_1[5:0]), .b(6'b100010), .eq(comparator_26_eq));  // open: gt, lt
  and and_8 (Output_14, _000000, comparator_27_eq);
  Comparator #(.width(6)) comparator_27 (.a(in_1[5:0]), .b(6'b011000), .eq(comparator_27_eq));  // open: gt, lt
  and and_9 (Output_16, _000000, comparator_28_eq);
  Comparator #(.width(6)) comparator_28 (.a(in_1[5:0]), .b(6'b011001), .eq(comparator_28_eq));  // open: gt, lt
  and and_10 (Output_18, _000000, comparator_29_eq);
  Comparator #(.width(6)) comparator_29 (.a(in_1[5:0]), .b(6'b011010), .eq(comparator_29_eq));  // open: gt, lt
  and and_11 (Output_20, _000000, comparator_30_eq);
  Comparator #(.width(6)) comparator_30 (.a(in_1[5:0]), .b(6'b011011), .eq(comparator_30_eq));  // open: gt, lt
  and and_12 (Output_8, _000000, comparator_31_eq);
  Comparator #(.width(6)) comparator_31 (.a(in_1[5:0]), .b(6'b101010), .eq(comparator_31_eq));  // open: gt, lt
  and and_13 (Output_25, comparator_20_eq, comparator_21_eq);
  and and_14 (Output_29, comparator_22_eq, comparator_23_eq);
  Comparator #(.width(6)) comparator_32 (.a(in_1[5:0]), .b(6'b101011), .eq(comparator_32_eq));  // open: gt, lt
  Comparator #(.width(6)) comparator_33 (.a(in_1[5:0]), .b(6'b100100), .eq(comparator_33_eq));  // open: gt, lt
  Comparator #(.width(6)) comparator_34 (.a(in_1[5:0]), .b(6'b100101), .eq(comparator_34_eq));  // open: gt, lt
  Comparator #(.width(6)) comparator_35 (.a(in_1[5:0]), .b(6'b100111), .eq(comparator_35_eq));  // open: gt, lt
  Comparator #(.width(6)) comparator_36 (.a(in_1[5:0]), .b(6'b101000), .eq(comparator_36_eq));  // open: gt, lt
  Comparator #(.width(6)) comparator_37 (.a(in_1[5:0]), .b(6'b001000), .eq(comparator_37_eq));  // open: gt, lt
  Comparator #(.width(6)) comparator_38 (.a(in_1[5:0]), .b(6'b010000), .eq(comparator_38_eq));  // open: gt, lt
  Comparator #(.width(6)) comparator_39 (.a(in_1[5:0]), .b(6'b010010), .eq(comparator_39_eq));  // open: gt, lt
  and and_15 (Output_10, _000000, comparator_32_eq);
  and and_16 (Output_12, _000000, comparator_33_eq);
  and and_17 (Output_15, _000000, comparator_34_eq);
  and and_18 (Output_17, _000000, comparator_35_eq);
  and and_19 (Output_19, _000000, comparator_36_eq);
  and and_20 (Output_33, _000000, comparator_37_eq);
  and and_21 (Output_37, _000000, comparator_38_eq);
  and and_22 (Output_41, _000000, comparator_39_eq);
  Comparator #(.width(6)) comparator_40 (.a(in_1[31:26]), .b(6'b000010), .eq(Output_13));  // open: gt, lt

  assign Output = in_1[25:21];
  assign Output_2 = in_1[5:0];
  assign Output_3 = in_1[25:0];
  assign Output_4 = in_1[20:16];
  assign Output_5 = in_1[15:0];
  assign Output_6 = in_1[15:11];

  // Other names for the same wires on the sheet: add = Output_9; addi = Output_21; and = Output_12; andi = Output_31;
  //   beq = Output_24; bgtz = Output_36; blez = Output_32; bltz = Output_40; bne = Output_28; div = Output_18;
  //   divu = Output_20; halt = Output_26; Const[15:0] = in_1[15:0]; FC[5:0] = in_1[5:0]; Salto[25:0] = in_1[25:0];
  //   RD[4:0] = in_1[15:11]; RT[4:0] = in_1[20:16]; RS[4:0] = in_1[25:21]; OpCode[5:0] = in_1[31:26]; j = Output_13;
  //   jr = Output_33; kbd = Output_38; lw = Output_42; mfhi = Output_37; mflo = Output_41; mult = Output_14;
  //   mulu = Output_16; nop = Output_7; nor = Output_17; or = Output_15; ori = Output_35; pop = Output_25;
  //   push = Output_29; rnd = Output_34; slt = Output_8; slti = Output_23; sltiu = Output_27; sltu = Output_10;
  //   sub = Output_11; sw = Output_22; tty = Output_30; xor = Output_19; xori = Output_39

  // Notes on the sheet:
  //   Particionar Instruccion
  //   Instrucciones De Tipo I:
  //   Instrucciones De Tipo R
  //   Instrucciones DeTipo J
endmodule

module AluSelector (
  input  in_1,
  input  in_2,
  input  in_3,
  input  in_4,
  input  in_5,
  input  in_6,
  input  in_7,
  input  in_8,
  input  in_9,
  input  in_10,
  input  in_11,
  input  in_12,
  input  in_13,
  input  in_14,
  input  in_15,
  input  in_16,
  input  in_17,
  input  in_18,
  output [3:0] Output,
  output Output_2,
  output Output_3
);

  wire Add, And, Div, Mult, Or, or_2_out, Slt, Xor;

  or or_1 (Output_2, in_13, in_16, in_17, in_18, or_2_out);
  or or_2 (or_2_out, in_14, in_15);
  or or_3 (Add, in_1, in_13);
  or or_4 (Mult, in_3, in_4);
  or or_5 (Div, in_5, in_6);
  or or_6 (And, in_9, in_16);
  or or_7 (Slt, in_7, in_8, in_14, in_15);
  or or_8 (Or, in_10, in_17);
  or or_9 (Xor, in_12, in_18);
  or or_10 (Output_3, in_4, in_6, in_8, in_15);
  Priority_Encoder #(.select(4)) priority_encoder_1 (
    .in0(Add), .in1(in_2), .in2(Mult), .in3(Div), .in4(And), .in5(Or), .in6(in_11), .in7(Xor), .in8(Slt),
    .out(Output));  // open: in9, in10, in11, in12, in13, in14, in15, gs, en_out, en_in

  // Other names for the same wires on the sheet: add_t = in_1; addi = in_13; and_t = in_9; andi = in_16; div_t = in_5;
  //   divu = in_6; I_Op = Output_2; mult_t = in_3; mulu = in_4; nor = in_11; NoSign = Output_3; or_t = in_10;
  //   ori = in_17; slt_t = in_7; slti = in_14; sltiu = in_15; sltu = in_8; sub = in_2; xor_t = in_12; xori = in_18

  // Notes on the sheet:
  //   Operacion de Tipo I:
  //   Operaciones sin tener en cuenta el Signo:
endmodule

module ProgramCounter (
  input  in_1,
  input  in_2,
  input  in_3,
  input  [31:0] in_4,
  output [31:0] Output
);

  Register #(.width(32)) register_1 (.D(in_4), .en(in_2), .Q(Output), .clk(in_1), .clr(in_3));

  // Other names for the same wires on the sheet: Clk = in_1; enable = in_2; reset = in_3
endmodule

module BranchControl (
  input  [15:0] in_1,
  input  [31:0] InstActual,
  input  [25:0] Salto,
  input  [31:0] RS,
  input  [31:0] RT,
  input  in_6,
  input  in_7,
  input  in_8,
  input  in_9,
  input  in_10,
  input  in_11,
  input  in_12,
  input  in_13,
  output [31:0] Output
);

  wire and_1_out, and_2_out, and_3_out, and_4_out, and_5_out, comparator_1_eq, FC, RS_0, RS__0, RS__RT;
  wire [1:0] selector;
  wire [27:0] jmp;
  wire [31:0] IA_4, IA_4_CN;
  wire [31:18] CN;

  Comparator #(.width(32)) comparator_1 (.a({32{1'b0}}), .b(RS), .eq(comparator_1_eq), .lt(RS_0));  // open: gt
  or or_1 (RS__0, comparator_1_eq, RS_0);
  Comparator #(.width(32)) comparator_2 (.a(RS), .b(RT), .eq(RS__RT));  // open: gt, lt
  and and_1 (and_1_out, RS__RT, in_6);
  and and_2 (and_2_out, ~RS__RT, in_7);  // AND_Gate
  and and_3 (and_3_out, RS__0, in_8);
  and and_4 (and_4_out, ~RS__0, in_9);  // AND_Gate
  and and_5 (and_5_out, RS_0, in_10);
  or or_2 (FC, and_1_out, and_2_out, and_3_out, and_4_out, and_5_out);
  Adder #(.width(32)) adder_1 (.a(InstActual), .b(32'h4), .out(IA_4));  // open: cin, cout
  assign CN = {{13{in_1[15]}}, in_1[15]};  // Bit_Extender bit_extender_1
  Adder #(.width(32)) adder_2 (.a(IA_4), .b({CN, in_1, 2'b00}), .out(IA_4_CN));  // open: cin, cout
  Demultiplexer #(.select(2), .width(32), .enable("false")) demultiplexer_1 (
    .out0(IA_4), .out1(IA_4_CN), .out2({InstActual[31:28], jmp}), .out3(RS), .in(Output), .sel(selector));
  Priority_Encoder #(.select(2)) priority_encoder_1 (
    .in0(in_13), .in1(FC), .in2(in_12), .in3(in_11), .out(selector));  // open: gs, en_out, en_in
  // also tied to GND on the sheet: {jmp[0], jmp[1]}

  // Other names for the same wires on the sheet: beq = in_6; bgtz = in_9; blez = in_8; bltz = in_10; bne = in_7;
  //   CN[17:2] = in_1; const[15:0] = in_1; IA[31:0] = InstActual; j = in_12; salto_t[25:0] = jmp[27:2];
  //   jmp[31:28] = InstActual[31:28]; jr = in_11; nop = in_13
endmodule

module DataPath (
  input  in_1,
  input  in_2,
  input  [31:0] in_3,
  input  in_4,
  input  in_5,
  input  in_6
);

  wire Add, Addi, And, Andi, beq, bgtz, blez, bltz, bne, Div, Divu, j, jr, Mult, Mulu, nop, Nor, Or, Ori,
       Slt, Slti, Sltiu, Sltu, Sub, Xor, Xori;
  wire [15:0] Const;
  wire [25:0] Salto;
  wire [31:0] instructioncatcher_1_output, PC_In, PC_Out, RS, RT;

  InstructionCatcher instructioncatcher_1 (
    .in_1(in_1), .in_2(in_4), .in_3(in_6), .in_4(in_3), .Output(instructioncatcher_1_output));
  AluSelector aluselector_1 (
    .in_1(Add), .in_2(Sub), .in_3(Mult), .in_4(Mulu), .in_5(Div), .in_6(Divu), .in_7(Slt), .in_8(Sltu),
    .in_9(And), .in_10(Or), .in_11(Nor), .in_12(Xor), .in_13(Addi), .in_14(Slti), .in_15(Sltiu),
    .in_16(Andi), .in_17(Ori), .in_18(Xori));  // open: Output, Output_2, Output_3
  ProgramCounter programcounter_1 (.in_1(in_1), .in_2(in_4), .in_3(in_6), .in_4(PC_In), .Output(PC_Out));
  BranchControl branchcontrol_1 (
    .in_1(Const), .InstActual(PC_Out), .Salto(Salto), .RS(RS), .RT(RT), .in_6(beq), .in_7(bne), .in_8(blez),
    .in_9(bgtz), .in_10(bltz), .in_11(jr), .in_12(j), .in_13(nop), .Output(PC_In));

  // Other names for the same wires on the sheet: Clk = in_1; Enable = in_6; EnPC = in_5; Instruction[31:0] = in_3;
  //   Reset = in_4; W_R = in_2

  // Notes on the sheet:
  //   Inputs:
endmodule

module InstructionCatcher (
  input  in_1,
  input  in_2,
  input  in_3,
  input  [31:0] in_4,
  output [31:0] Output
);

  Register #(.width(32)) register_1 (
    .D(in_4), .en(in_3), .Q({Output[7:0], Output[15:8], Output[23:16], Output[31:24]}), .clk(in_1), .clr(in_2));

  // Other names for the same wires on the sheet: clock = in_1; enable = in_3; instruction[31:0] = in_4; reset = in_2
endmodule
